# Fritzing sketch Schets_fritzing (saved by Fritzing 0.9.3b)
breadboards: 1

parts:
  WeMos_D1_Mini1 = WeMos D1 Mini
  DRV_1 = DRV 8825 Stepper Motor Carrier, High Current [part_number="DRV 8825"]
  C1 = Capacitor Polarized [package=panasonic_d]
  M1 = Stepper Motor - Bipolar
  DHT1 = DHT11 Humitidy and Temperature Sensor
  HC-SR04_Sensor_1 = HC-SR04 Ultrasonic Distance Sensor
  Onderdeel1 = Soil Moisture Sensor
  U1 = mystery part, 3 pins [chip_label=LDR]
  R1 = Resistor [tolerance=±5% resistance=10 package="0402 [SMD]"]

nets:
  VCC: WeMos_D1_Mini1.5V, DRV_1.MS1, DRV_1.RESET, HC-SR04_Sensor_1.VCC, Onderdeel1.VCC, U1.pin2
  N1: WeMos_D1_Mini1.A0, Onderdeel1.SIG
  N2: WeMos_D1_Mini1.D0, U1.pin1
  N3: WeMos_D1_Mini1.D1, DRV_1.STEP
  N4: WeMos_D1_Mini1.D2, DRV_1.SLEEP
  N5: WeMos_D1_Mini1.D3, DRV_1.DIRECTION
  N6: WeMos_D1_Mini1.D4, R1.Pin_1
  N7: WeMos_D1_Mini1.D5, DHT1.DATA
  N8: WeMos_D1_Mini1.D6, DHT1.VDD
  N9: WeMos_D1_Mini1.D7, HC-SR04_Sensor_1.ECHO
  N10: WeMos_D1_Mini1.D8, HC-SR04_Sensor_1.TRIG
  GND: WeMos_D1_Mini1.G, DRV_1.MS2, DRV_1.MS3, DRV_1.GROUND_ST/_MT, C1.-, DHT1.GND, HC-SR04_Sensor_1.GND, Onderdeel1.GND, U1.pin3, R1.Pin_0
  N11: DRV_1.VOLTAGE_ST/_MT, C1.+
  N12: DRV_1.OUT_2B, M1.A
  N13: DRV_1.OUT_2A, M1.C
  N14: DRV_1.OUT_1A, M1.D
  N15: DRV_1.OUT_1B, M1.B

notes:
  External 12V

custom parts:
  WeMos D1 Mini: The D1 mini is a mini wifi board based on ESP-8266EX.
  DHT11 Humitidy and Temperature Sensor: DHT11 Humidity and Temperature Sensor
